# Fritzing sketch GATE CRYSTAL (saved by Fritzing 0.9.3b)
circuit board: 9.9616cm x 5.07225cm
breadboards: 1

parts:
  midi_in = MIDI_CONN_FEMALE_SUPPORT [package=din_5_female_support]
  S33 = Pushbutton [package="[THT]"]
  S34 = SWITCH-MOMENTARY-2 [package=tactile-pth-12mm]
  S36 = Pushbutton [package="[THT]"]
  S38 = SWITCH-MOMENTARY-2 [package=tactile-pth-12mm]
  4n28! = IC, DIP package, 6 pins [chip_label=IC]
  3_3k = Resistor [tolerance=±5% resistance=3.3k package=THT]
  R6 = Resistor [tolerance=±5% resistance=220 package=THT]
  100k = Resistor [tolerance=±5% resistance=100k package=THT]
  1N4148 = Rectifier Diode [part_number=1N4001 package="300 mil [THT]"]
  Pro_Micro = IC, DIP package, 24 pins [chip_label="Pro Micro"]
  S40 = Pushbutton [package="[THT]"]
  S41 = SWITCH-MOMENTARY-2 [package=tactile-pth-12mm]
  LED3 = LED - 5mm [color="Red (633nm)" package="5 mm [THT]"]
  S43 = Pushbutton [package="[THT]"]
  OUTPUT = AUDIO-JACK2_multicolor_2holestress [package="audio-jack (multicolor)"]
  BIT_IO = AUDIO-JACK2_multicolor_2holestress [package="audio-jack (multicolor)"]
  BYTE_IN = AUDIO-JACK2_multicolor_2holestress [package="audio-jack (multicolor)"]
  S44 = Pushbutton [package="[THT]"]
  KNOB_1 = Rotary Potentiometer (Small) [maximum_resistance=100kΩ package=THT]
  KNOB_2 = Rotary Potentiometer (Small) [maximum_resistance=100kΩ package=THT]
  KNOB_3 = Rotary Potentiometer (Small) [maximum_resistance=100kΩ package=THT]
  KNOB_0 = Rotary Potentiometer (Small) [maximum_resistance=100kΩ package=THT]
  R7 = Resistor [tolerance=±5% resistance=220 package=THT]
  SJ2 = Solder Jumper [package=sj_2s-no]
  R8 = Resistor [tolerance=±5% resistance=1k package=THT]
  R9 = Resistor [tolerance=±5% resistance=1k package=THT]
  LED2 = LED - 5mm [color="Red (633nm)" package="5 mm [THT]"]
  LED4 = LED - 5mm [color="Red (633nm)" package="5 mm [THT]"]
  LED5 = LED - 5mm [color="Red (633nm)" package="5 mm [THT]"]
  R10 = Resistor [tolerance=±5% resistance=1k package=THT]
  R11 = Resistor [tolerance=±5% resistance=1k package=THT]
  LED6 = LED - 5mm [color="Red (633nm)" package="5 mm [THT]"]
  R12 = Resistor [tolerance=±5% resistance=1k package=THT]
  9-12V_in = female pin header, 2 pins [form="♀ (female)"]
  D8 = female pin header, 2 pins [form="♀ (female)"]
  C1 = Ceramic Capacitor [capacitance=100nF package="100 mil [THT, multilayer]"]
  J1 = shrouded pin header, 6 pins [form="♂ (shrouded male)"]
  1k = Resistor [tolerance=±5% resistance=1k package=THT]
  +____-PLED = female pin header, 2 pins [form="♀ (female)"]
  R13 = Resistor [tolerance=±5% resistance=1k package=THT]
  +txl- = female pin header, 2 pins [form="♀ (female)"]

nets:
  N1: midi_in.MIDI_IN, 4n28!.pin2, 1N4148.anode
  N2: midi_in.MIDI_OUT, R6.Pin_0
  N3: S33.Pin_1, S33.Pin_2, S34.2, Pro_Micro.pin9
  N4: S33.Pin_3, S33.Pin_4, S34.1, S36.Pin_3, S36.Pin_4, S38.1, 4n28!.pin4, 100k.Pin_0, Pro_Micro.pin3, Pro_Micro.pin4, Pro_Micro.pin23, S40.Pin_3, S40.Pin_4, S41.1, S43.Pin_1, S43.Pin_2, OUTPUT.SLEEVE, BIT_IO.SLEEVE, BYTE_IN.SLEEVE, S44.Pin_1, S44.Pin_2, KNOB_1.leg1, KNOB_2.leg1, KNOB_3.leg1, KNOB_0.leg1, R8.Pin_1, R9.Pin_0, R10.Pin_1, R11.Pin_1, R12.Pin_0, 9-12V_in.pin1, D8.pin1, C1.0, J1.pin4, 1k.Pin_0, R13.Pin_1
  N5: S36.Pin_1, S36.Pin_2, S38.2, Pro_Micro.pin7
  N6: 4n28!.pin1, R6.Pin_1, 1N4148.cathode
  N7: 4n28!.pin5, 3_3k.Pin_1, Pro_Micro.pin2
  N8: 4n28!.pin6, 100k.Pin_1
  N9: 3_3k.Pin_0, Pro_Micro.pin21, BYTE_IN.TIP, KNOB_1.leg2, KNOB_2.leg2, KNOB_3.leg2, KNOB_0.leg2, J1.pin6, +____-PLED.pin2
  N10: Pro_Micro.pin1, +txl-.pin2
  N11: Pro_Micro.pin5, LED3.anode
  N12: Pro_Micro.pin6, LED2.anode
  N13: Pro_Micro.pin8, S44.Pin_3, S44.Pin_4
  N14: Pro_Micro.pin10, S43.Pin_3, S43.Pin_4
  N15: Pro_Micro.pin11, S40.Pin_1, S40.Pin_2, S41.2
  N16: Pro_Micro.pin12, R7.Pin_1
  N17: Pro_Micro.pin13, BIT_IO.TIP, LED6.anode
  N18: Pro_Micro.pin14, D8.pin2, J1.pin5
  N19: Pro_Micro.pin15, LED4.anode, J1.pin1
  N20: Pro_Micro.pin16, LED5.anode, J1.pin2
  N21: Pro_Micro.pin17, BYTE_IN.RING
  N22: Pro_Micro.pin18, KNOB_1.wiper
  N23: Pro_Micro.pin19, KNOB_2.wiper
  N24: Pro_Micro.pin20, KNOB_3.wiper
  N25: Pro_Micro.pin22, J1.pin3
  N26: Pro_Micro.pin24, 9-12V_in.pin2
  N27: LED3.cathode, R8.Pin_0
  N28: OUTPUT.RING, SJ2.2
  N29: OUTPUT.TIP, R7.Pin_0, SJ2.1, C1.1
  N30: BYTE_IN.RSH, KNOB_0.wiper
  N31: R9.Pin_1, LED2.cathode
  N32: LED4.cathode, R10.Pin_0
  N33: LED5.cathode, R11.Pin_0
  N34: LED6.cathode, R12.Pin_1
  N35: 1k.Pin_1, +____-PLED.pin1
  N36: R13.Pin_0, +txl-.pin1

notes:
  V3

custom parts:
  AUDIO-JACK2_multicolor_2holestress: Stereo audio jack with bypass switches.
